// Digital circuit CPU.dig as structural Verilog
module CPU (
);

  Ring_Counter ring_counter_1 ();  // open: Clk, Clr, Q0, Q1, Q2, Q3, Q4, Q5
  Memory_Address_Register memory_address_register_1 ();  // open: NLm, Clk, I0, I1, I2, I3, S0, S1, S2, S3, S4, S5, S6, S7
  Instruction_Register instruction_register_1 ();  // open: NEi, Clr, Clk, NLi, I0, I1, I2, I3, I4, I5, I6, I7, C0, C1, C2, C3, Op0, Op1, Op2, Op3
  Register_B register_b_1 ();  // open: NLb, Clk, I0, I1, I2, I3, I4, I5, I6, I7, S0, S1, S2, S3, S4, S5, S6, S7
  Register_OUT register_out_1 ();  // open: NLo, Clk, I0, I1, I2, I3, I4, I5, I6, I7, S0, S1, S2, S3, S4, S5, S6, S7
  Acumulator acumulator_1 ();  // open: NLa, Ea, Clk, I0, I1, I2, I3, I4, I5, I6, I7, S0, S1, S2, S3, S4, S5, S6, S7
  ULA ula_1 ();  // open: A0, B0, A1, B1, A2, B2, A3, B3, A4, B4, A5, B5, A6, B6, A7, B7, C0, C1, C2, Eu, out_20, eq, plus, S0, S1, S2, S3, S4, S5, S6, S7
endmodule
